// Logisim project 1_Zadanie_Matusiskova_Maria.circ as structural Verilog: 1 circuit, main circuit main
module main (
  input  A,
  input  B,
  input  C,
  input  D,
  output Y,
  output Z,
  output Y_DNF,
  output Z_DNF,
  output Y_KNF,
  output Z_KNF
);

  wire A_B_C_nD_out, A_B_out, B_D_out, n_C_nD_out, nA_D_out, nA_nC_out, nA_out, nB_D_out, nB_nC_out, nB_out,
       nC_out, nD_out, or_1_out, or_2_out, or_3_out, or_4_out;

  not nA (nA_out, A);
  not nC (nC_out, C);
  not nB (nB_out, B);
  not nD (nD_out, D);
  and A_B (A_B_out, A, B);
  nand n_C_nD (n_C_nD_out, C, nD_out);
  or B_D (B_D_out, B, D);
  and nA_nC (nA_nC_out, nA_out, nC_out);
  and nA_D (nA_D_out, nA_out, D);
  and nB_nC (nB_nC_out, nB_out, nC_out);
  and nB_D (nB_D_out, nB_out, D);
  and A_B_C_nD (A_B_C_nD_out, A, B, C, nD_out);
  or or_1 (or_1_out, nA_out, nB_out, C);
  or or_2 (or_2_out, nA_out, nB_out, nD_out);
  or or_3 (or_3_out, A, nC_out, D);
  or or_4 (or_4_out, B, nC_out, D);
  xor xor_1 (Y, A_B_out, n_C_nD_out);
  nor nor_1 (Z, n_C_nD_out, B_D_out);
  or or_5 (Y_DNF, nA_nC_out, nA_D_out, nB_nC_out, nB_D_out, A_B_C_nD_out);
  and nB_C_nD (Z_DNF, C, nB_out, nD_out);
  and and_1 (Y_KNF, or_1_out, or_2_out, or_3_out, or_4_out);

  assign Z_KNF = Z_DNF;

  // Notes on the sheet:
  //   !(A.B).!(C.!D)+(A.B).!!(C.!D)
  //   !A+!B+C
  //   !A+!B+!D
  //   A+!C+D
  //   B+!C+D
  //   !(!(C.!D)+(B+D))
  //   (!A.!C)+(!A.D)+(!B.!C)+(!B.D)+(A.B.C.!D)
  //   (!A+!B+C).(!A+!B+!D).(A+!C+D).(B+!C+D)
endmodule
