// Logisim project 2_Zadanie_Matusiskova_Maria.circ as structural Verilog: 1 circuit, main circuit main
// !(!(!(A).!(B).!(C).D).!(B.C).!(!(B).C.!(D)).!(A.!(D)))
module main (
  input  a,
  input  b,
  input  c,
  input  d,
  output A_DNF,
  output B_DNF,
  output C_DNF,
  output D_DNF,
  output A_KNF,
  output B_KNF,
  output C_KNF,
  output D_KNF
);

  wire n_A_n_D_out, n_B_C_out, n_C_D_out, na_2_out, na_out, nand_1_out, nand_2_out, nand_3_out, nand_4_out,
       nb_2_out, nb_out, nc_2_out, nc_out, nd_2_out, nd_out, nor_1_out, nor_2_out, nor_3_out, nor_4_out,
       nor_5_out, nor_6_out, nor_7_out, nor_8_out;

  nor na (na_out, a, a);
  nand nb (nb_out, b, b);
  nand na_2 (na_2_out, a, a);
  nor nb_2 (nb_2_out, b, b);
  nand nc (nc_out, c, c);
  nor nc_2 (nc_2_out, c, c);
  nand nd (nd_out, d, d);
  nor nd_2 (nd_2_out, d, d);
  nand n_C_D (n_C_D_out, c, d);
  nand nand_1 (nand_1_out, b, nc_out, nd_out);
  nand nand_2 (nand_2_out, nb_out, c, nd_out);
  nand nand_3 (nand_3_out, na_2_out, nb_out, nc_out, d);
  nand n_B_C (n_B_C_out, b, c);
  nand nand_4 (nand_4_out, nb_out, c, nd_out);
  nand n_A_n_D (n_A_n_D_out, a, nd_out);
  nor nor_1 (nor_1_out, a, b);
  nor nor_2 (nor_2_out, a, b, c);
  nor nor_3 (nor_3_out, a, c, nd_2_out);
  nor nor_4 (nor_4_out, nb_2_out, nc_2_out, d);
  nor nor_5 (nor_5_out, a, c, d);
  nor nor_6 (nor_6_out, a, nb_2_out, c);
  nor nor_7 (nor_7_out, na_out, b, nd_2_out);
  nor nor_8 (nor_8_out, b, nc_2_out, nd_2_out);
  nand nand_5 (B_DNF, na_2_out, nb_out);
  nand nand_6 (C_DNF, na_2_out, n_C_D_out, nand_1_out, nand_2_out);
  nand nand_7 (D_DNF, nand_3_out, n_B_C_out, nand_4_out, n_A_n_D_out);
  nor nor_9 (B_KNF, nor_1_out, nor_1_out);
  nor nor_10 (C_KNF, nor_2_out, nor_3_out, nor_4_out);
  nor nor_11 (D_KNF, nor_5_out, nor_6_out, nor_7_out, nor_8_out);

  assign A_DNF = a;
  assign A_KNF = a;

  // Notes on the sheet:
  //   !(B.!(C).!(D))
  //   !(!(B).C.!(D))
  //   !(!(A).!(B).!(C).D)
  //   !(!(B).C.!(D))
  //   !(A+B)
  //   !(A+B+C)
  //   !(A+C+!(D))
  //   !(!(B)+!(C)+D)
  //   !(A+C+D)
  //   !(A+!(B)+C)
  //   !(!(A)+B+!(D))
  //   !(B+!(C)+!(D))
  //   !(!(A).!(B))
  //   !!(A+B)
  //   !(!(A).!(C.D).!(B.!(C).!(D)).!(!(B).C.!(D)))
  //   !(!(!(A).!(B).!(C).D).!(B.C).!(!(B).C.!(D)).!(A.!(D)))
  //   !(!(A+B+C)+!(A+C+!(D))+!(!(B)+!(C)+!(D)))
  //   !(!(A+C+D)+!(A+!(B)+C)+(!(A)+B+D)+!(B+!(C)+!(D)))
endmodule
