// Logisim project 3_Zadanie_Matusiskova_Maria.circ as structural Verilog: 1 circuit, main circuit main
module main (
  input  x,
  input  Res,
  output Y
);

  wire CLK_out, nand_1_out, nand_2_out, nand_3_out, nand_4_out, X_out, X_Z1_Z2_out, X_Z2_nZ3_out, Z1_q,
       Z1_X_out, Z1_Z3_out, Z2_q, Z2_Z3_out, Z3_q, Z3_qn;

  nand u_X (X_out, x, x);
  Clock CLK (.out(CLK_out));
  nand X_Z2_nZ3 (X_Z2_nZ3_out, x, Z2_q, Z3_qn);
  nand Z2_Z3 (Z2_Z3_out, Z2_q, Z3_q);
  nand X_Z1_Z2 (X_Z1_Z2_out, x, Z1_q, Z2_q);
  nand nand_1 (nand_1_out, X_Z2_nZ3_out, Z2_Z3_out);
  nand nand_2 (nand_2_out, X_out, Z1_q);
  nand nand_3 (nand_3_out, X_Z1_Z2_out, X_Z1_Z2_out);
  nand Z1_Z3 (Z1_Z3_out, Z1_q, Z3_q);
  nand nand_4 (nand_4_out, X_Z2_nZ3_out, X_out);
  nand Z1_X (Z1_X_out, Z1_q, x);
  nand nand_5 (Y, Z1_Z3_out, Z1_Z3_out);
  J_K_Flip_Flop Z1 (.J(nand_1_out), .clk(CLK_out), .K(nand_4_out), .Q(Z1_q), .reset(Res));  // open: Qn, preset, en
  J_K_Flip_Flop Z2 (.J(nand_2_out), .clk(CLK_out), .K(x), .Q(Z2_q), .reset(Res));  // open: Qn, preset, en
  J_K_Flip_Flop Z3 (
    .J(nand_3_out), .clk(CLK_out), .K(Z1_X_out), .Q(Z3_q), .Qn(Z3_qn), .reset(Res));  // open: preset, en
endmodule
